// Digital circuit Rangkaian Digital Latihan 1.dig as structural Verilog
module Rangkaian_Digital_Latihan_1 (
  input  CL,
  input  A
);

  wire nand_1_out, nor_1_out;

  nand nand_1 (nand_1_out, CL, A);
  nor nor_1 (nor_1_out, CL, A);
  LED led_1 (.in(nand_1_out));
  LED LED_2 (.in(nand_1_out));
  LED led_3 (.in(nor_1_out));
  LED led_4 (.in(nor_1_out));

  // Notes on the sheet:
  //   CL: Hz: 50
endmodule
